// Logisim project MIPS PC.circ as structural Verilog: 5 circuits, main circuit main
module main (
);

  wire alu_1_zero, and_1_out, clock_1_out, control_1_alusrc, control_1_branch, control_1_jump,
       control_1_memtoreg, control_1_memwrite, control_1_regdst, control_1_regwrite, control_1_shift,
       control_1_z, xor_1_out;
  wire [2:0] control_1_alucon;
  wire [3:0] if_1__3_0, if_1__7_4, if_1__11_8, if_1__15_12, if_1__19_16, multiplexer_1_out;
  wire [7:0] adder_1_out, adder_2_out, alu_1_aluresult, bit_extender_1_out, if_1__7_0, if_1__15_8,
       multiplexer_2_out, multiplexer_3_out, multiplexer_4_out, multiplexer_5_out, multiplexer_6_out, PC_q,
       ram_1_data, registers_1_read_data_1, registers_1_read_data_2;

  Register PC (.D(multiplexer_5_out), .Q(PC_q), .clk(clock_1_out));  // open: en, clr
  Adder adder_1 (.a(8'h1), .b(PC_q), .out(adder_1_out));  // open: cin, cout
  IF if_1 (
    .A(PC_q), ._3_0(if_1__3_0), ._7_4(if_1__7_4), ._11_8(if_1__11_8), ._15_12(if_1__15_12),
    ._19_16(if_1__19_16), ._7_0(if_1__7_0), ._15_8(if_1__15_8));
  Control control_1 (
    ._19_16(if_1__19_16), .shift(control_1_shift), .branch(control_1_branch), .memWrite(control_1_memwrite),
    .RegWrite(control_1_regwrite), .MemtoReg(control_1_memtoreg), .ALUSrc(control_1_alusrc),
    .RegDst(control_1_regdst), .jump(control_1_jump), .ALUCon(control_1_alucon), .z(control_1_z));
  Multiplexer #(.width(4), .disabled(0), .enable("false")) multiplexer_1 (
    .in0(if_1__7_4), .in1(if_1__11_8), .out(multiplexer_1_out), .sel(control_1_regdst));
  assign bit_extender_1_out = {{4{1'b0}}, if_1__3_0};  // Bit_Extender bit_extender_1
  Registers registers_1 (
    .Write_Register(multiplexer_1_out), .Read_data_1(registers_1_read_data_1), .Writedata(multiplexer_6_out),
    .Read_data_2(registers_1_read_data_2), .Read_register_1(if_1__15_12), .Read_register_2(if_1__11_8),
    .regWrite(control_1_regwrite));
  Clock clock_1 (.out(clock_1_out));
  Multiplexer #(.width(8), .disabled(0), .enable("false")) multiplexer_2 (
    .in0(registers_1_read_data_1), .in1(bit_extender_1_out), .out(multiplexer_2_out), .sel(control_1_shift));
  Multiplexer #(.width(8), .disabled(0), .enable("false")) multiplexer_3 (
    .in0(registers_1_read_data_2), .in1(if_1__7_0), .out(multiplexer_3_out), .sel(control_1_alusrc));
  Adder adder_2 (.a(adder_1_out), .b(if_1__7_0), .out(adder_2_out));  // open: cin, cout
  and and_1 (and_1_out, control_1_branch, xor_1_out);
  xor xor_1 (xor_1_out, control_1_z, alu_1_zero);
  ALU alu_1 (
    .A(multiplexer_2_out), .B(multiplexer_3_out), .ALUop(control_1_alucon), .Zero(alu_1_zero),
    .ALUresult(alu_1_aluresult));
  Multiplexer #(.width(8), .disabled(0), .enable("false")) multiplexer_4 (
    .in0(adder_1_out), .in1(adder_2_out), .out(multiplexer_4_out), .sel(and_1_out));
  Multiplexer #(.width(8), .disabled(0), .enable("false")) multiplexer_5 (
    .in0(multiplexer_4_out), .in1(if_1__15_8), .out(multiplexer_5_out), .sel(control_1_jump));
  RAM #(.bus("separate")) ram_1 (
    .addr(alu_1_aluresult), .din(registers_1_read_data_2), .data(ram_1_data), .str(control_1_memwrite),
    .clk(clock_1_out), .ld(1'b1));  // open: sel, clr
  Multiplexer #(.width(8), .disabled(0), .enable("false")) multiplexer_6 (
    .in0(alu_1_aluresult), .in1(ram_1_data), .out(multiplexer_6_out), .sel(control_1_memtoreg));
endmodule

module IF (
  input  [7:0] A,
  output [3:0] _3_0,
  output [3:0] _7_4,
  output [3:0] _11_8,
  output [3:0] _15_12,
  output [3:0] _19_16,
  output [7:0] _7_0,
  output [7:0] _15_8
);

  ROM #(.dataWidth(20)) rom_1 (.addr(A), .data({_19_16, _15_8[7:4], _11_8, _7_0[7:4], _3_0}));  // open: sel

  assign _7_0[3:0] = _3_0;
  assign _7_4 = _7_0[7:4];
  assign _15_8[3:0] = _11_8;
  assign _15_12 = _15_8[7:4];

  // Notes on the sheet:
  //   contents of rom_1 (hex, n*v repeats v):
  //   60105 51205 b1240 e1401 d1300 a0152 25420 2150 f5420 32200 c2114 72103 92203 40221 d1200 7f2fc 9f1fc
  //   d1300 121fc
endmodule

// Reg
module Registers (
  input  [7:0] Writedata,
  input  [3:0] Read_register_1,
  input  [3:0] Read_register_2,
  input  regWrite,
  input  [3:0] Write_Register,
  output [7:0] Read_data_1,
  output [7:0] Read_data_2
);

  wire and_1_out, clock_1_out, decoder_1_out1, decoder_1_out2, decoder_1_out3, decoder_1_out4,
       decoder_1_out5, decoder_1_out6, decoder_1_out7, decoder_1_out8, decoder_1_out9, decoder_1_out10,
       decoder_1_out11, decoder_1_out12, decoder_1_out13, decoder_1_out14, decoder_1_out15;
  wire [7:0] multiplexer_2_out, multiplexer_3_out, multiplexer_4_out, multiplexer_5_out, multiplexer_6_out,
       multiplexer_7_out, multiplexer_8_out, multiplexer_9_out, multiplexer_10_out, multiplexer_11_out,
       multiplexer_12_out, multiplexer_13_out, multiplexer_14_out, multiplexer_15_out, multiplexer_16_out,
       s0_q, s1_q, s2_q, s3_q, s4_q, s5_q, s6_q, s7_q, sp_q, t0_q, t1_q, t2_q, t3_q, t4_q, t5_q, zero_q;

  Multiplexer #(.select(4), .width(8), .disabled(0), .enable("false")) multiplexer_1 (
    .in0(zero_q), .in1(t0_q), .in2(t1_q), .in3(t2_q), .in4(t3_q), .in5(t4_q), .in6(t5_q), .in7(s0_q),
    .in8(s1_q), .in9(s2_q), .in10(s3_q), .in11(s4_q), .in12(s5_q), .in13(s6_q), .in14(s7_q), .in15(sp_q),
    .out(Read_data_1), .sel(Read_register_1));
  Clock clock_1 (.out(clock_1_out));
  and and_1 (and_1_out, clock_1_out, regWrite);
  Register zero (.D({8{1'b0}}), .Q(zero_q), .clk(and_1_out));  // open: en, clr
  Multiplexer #(.width(8), .disabled(0), .enable("false")) multiplexer_2 (
    .in0(s1_q), .in1(Writedata), .out(multiplexer_2_out), .sel(decoder_1_out8));
  Register s1 (.D(multiplexer_2_out), .Q(s1_q), .clk(and_1_out));  // open: en, clr
  Multiplexer #(.width(8), .disabled(0), .enable("false")) multiplexer_3 (
    .in0(s5_q), .in1(Writedata), .out(multiplexer_3_out), .sel(decoder_1_out12));
  Register s5 (.D(multiplexer_3_out), .Q(s5_q), .clk(and_1_out));  // open: en, clr
  Register t3 (.D(multiplexer_4_out), .Q(t3_q), .clk(and_1_out));  // open: en, clr
  Multiplexer #(.width(8), .disabled(0), .enable("false")) multiplexer_4 (
    .in0(t3_q), .in1(Writedata), .out(multiplexer_4_out), .sel(decoder_1_out4));
  Multiplexer #(.width(8), .disabled(0), .enable("false")) multiplexer_5 (
    .in0(t0_q), .in1(Writedata), .out(multiplexer_5_out), .sel(decoder_1_out1));
  Multiplexer #(.width(8), .disabled(0), .enable("false")) multiplexer_6 (
    .in0(t4_q), .in1(Writedata), .out(multiplexer_6_out), .sel(decoder_1_out5));
  Multiplexer #(.width(8), .disabled(0), .enable("false")) multiplexer_7 (
    .in0(s2_q), .in1(Writedata), .out(multiplexer_7_out), .sel(decoder_1_out9));
  Multiplexer #(.width(8), .disabled(0), .enable("false")) multiplexer_8 (
    .in0(s6_q), .in1(Writedata), .out(multiplexer_8_out), .sel(decoder_1_out13));
  Register t0 (.D(multiplexer_5_out), .Q(t0_q), .clk(and_1_out));  // open: en, clr
  Register t4 (.D(multiplexer_6_out), .Q(t4_q), .clk(and_1_out));  // open: en, clr
  Register s2 (.D(multiplexer_7_out), .Q(s2_q), .clk(and_1_out));  // open: en, clr
  Register s6 (.D(multiplexer_8_out), .Q(s6_q), .clk(and_1_out));  // open: en, clr
  Decoder #(.select(4), .disabled(0), .enable("false")) decoder_1 (
    .out1(decoder_1_out1), .out2(decoder_1_out2), .out3(decoder_1_out3), .out4(decoder_1_out4),
    .out5(decoder_1_out5), .out6(decoder_1_out6), .out7(decoder_1_out7), .out8(decoder_1_out8),
    .out9(decoder_1_out9), .out10(decoder_1_out10), .out11(decoder_1_out11), .out12(decoder_1_out12),
    .out13(decoder_1_out13), .out14(decoder_1_out14), .out15(decoder_1_out15), .sel(Write_Register));  // open: out0
  Register #(.trigger("falling")) t1 (.D(multiplexer_9_out), .Q(t1_q), .clk(and_1_out));  // open: en, clr
  Multiplexer #(.width(8), .disabled(0), .enable("false")) multiplexer_9 (
    .in0(t1_q), .in1(Writedata), .out(multiplexer_9_out), .sel(decoder_1_out2));
  Multiplexer #(.width(8), .disabled(0), .enable("false")) multiplexer_10 (
    .in0(t5_q), .in1(Writedata), .out(multiplexer_10_out), .sel(decoder_1_out6));
  Multiplexer #(.width(8), .disabled(0), .enable("false")) multiplexer_11 (
    .in0(s3_q), .in1(Writedata), .out(multiplexer_11_out), .sel(decoder_1_out10));
  Multiplexer #(.width(8), .disabled(0), .enable("false")) multiplexer_12 (
    .in0(s7_q), .in1(Writedata), .out(multiplexer_12_out), .sel(decoder_1_out14));
  Register t5 (.D(multiplexer_10_out), .Q(t5_q), .clk(and_1_out));  // open: en, clr
  Register s3 (.D(multiplexer_11_out), .Q(s3_q), .clk(and_1_out));  // open: en, clr
  Register s7 (.D(multiplexer_12_out), .Q(s7_q), .clk(and_1_out));  // open: en, clr
  Multiplexer #(.width(8), .disabled(0), .enable("false")) multiplexer_13 (
    .in0(t2_q), .in1(Writedata), .out(multiplexer_13_out), .sel(decoder_1_out3));
  Register t2 (.D(multiplexer_13_out), .Q(t2_q), .clk(and_1_out));  // open: en, clr
  Multiplexer #(.width(8), .disabled(0), .enable("false")) multiplexer_14 (
    .in0(s0_q), .in1(Writedata), .out(multiplexer_14_out), .sel(decoder_1_out7));
  Register s0 (.D(multiplexer_14_out), .Q(s0_q), .clk(and_1_out));  // open: en, clr
  Register s4 (.D(multiplexer_15_out), .Q(s4_q), .clk(and_1_out));  // open: en, clr
  Multiplexer #(.width(8), .disabled(0), .enable("false")) multiplexer_15 (
    .in0(s4_q), .in1(Writedata), .out(multiplexer_15_out), .sel(decoder_1_out11));
  Register sp (.D(multiplexer_16_out), .Q(sp_q), .clk(and_1_out));  // open: en, clr
  Multiplexer #(.width(8), .disabled(0), .enable("false")) multiplexer_16 (
    .in0(sp_q), .in1(Writedata), .out(multiplexer_16_out), .sel(decoder_1_out15));
  Multiplexer #(.select(4), .width(8), .disabled(0), .enable("false")) multiplexer_17 (
    .in0(zero_q), .in1(t0_q), .in2(t1_q), .in3(t2_q), .in4(t3_q), .in5(t4_q), .in6(t5_q), .in7(s0_q),
    .in8(s1_q), .in9(s2_q), .in10(s3_q), .in11(s4_q), .in12(s5_q), .in13(s6_q), .in14(s7_q), .in15(sp_q),
    .out(Read_data_2), .sel(Read_register_2));
endmodule

module ALU (
  input  [7:0] A,
  input  [7:0] B,
  input  [2:0] ALUop,
  output Zero,
  output [7:0] ALUresult
);

  wire comparator_1_lt;
  wire [2:0] bit_extender_2_out;
  wire [7:0] adder_1_out, and_1_out, bit_extender_1_out, multiplexer_1_out, not_1_out, or_1_out,
       shifter_1_out, shifter_2_out, xor_1_out;

  assign bit_extender_1_out = {{7{ALUop[0]}}, ALUop[0]};  // Bit_Extender bit_extender_1
  Comparator #(.mode("unsigned")) comparator_1 (.a(A), .b(8'h8), .lt(comparator_1_lt));  // open: gt, eq
  assign xor_1_out = B ^ bit_extender_1_out;  // XOR_Gate xor_1, 8 bits wide
  Multiplexer #(.width(8), .disabled(0), .enable("false")) multiplexer_1 (
    .in0({8{1'b0}}), .in1(B), .out(multiplexer_1_out), .sel(comparator_1_lt));
  Adder adder_1 (.a(A), .b(xor_1_out), .out(adder_1_out), .cin(ALUop[0]));  // open: cout
  assign and_1_out = A & B;  // AND_Gate and_1, 8 bits wide
  assign or_1_out = A | B;  // OR_Gate or_1, 8 bits wide
  Bit_Extender #(.out_width(3), .\type ("sign")) bit_extender_2 (.in(A), .out(bit_extender_2_out));
  assign not_1_out = ~or_1_out;  // NOT_Gate not_1, 8 bits wide
  Shifter shifter_1 (.in(multiplexer_1_out), .\dist (bit_extender_2_out), .out(shifter_1_out));
  Shifter #(.shift("lr")) shifter_2 (.in(multiplexer_1_out), .\dist (bit_extender_2_out), .out(shifter_2_out));
  Multiplexer #(.select(3), .width(8), .disabled(0), .enable("false")) multiplexer_2 (
    .in0(adder_1_out), .in1(adder_1_out), .in2(and_1_out), .in3(or_1_out), .in4(not_1_out),
    .in5(shifter_1_out), .in6(shifter_2_out), .in7(shifter_2_out), .out(ALUresult), .sel(ALUop));
  Comparator #(.mode("unsigned")) comparator_2 (.a(ALUresult), .b({8{1'b0}}), .eq(Zero));  // open: gt, lt
endmodule

module Control (
  input  [3:0] _19_16,
  output shift,
  output branch,
  output memWrite,
  output RegWrite,
  output MemtoReg,
  output ALUSrc,
  output RegDst,
  output jump,
  output [2:0] ALUCon,
  output z
);

  ROM #(.addrWidth(4), .dataWidth(12)) rom_1 (
    .addr(_19_16), .data({z, ALUCon, jump, RegDst, ALUSrc, MemtoReg, RegWrite, memWrite, branch, shift}));  // open: sel

  // Notes on the sheet:
  //   contents of rom_1 (hex, n*v repeats v):
  //   308 902 108 268 609 168 68 64 208 78 509 8 368 80 102 408
endmodule
